// Logisim project exp1_2a.circ as structural Verilog: 1 circuit, main circuit main
module main (
  input  a,
  input  b,
  input  c,
  output t
);

  wire and_1_out, and_2_out, and_3_out;

  and and_1 (and_1_out, a, b);
  and and_2 (and_2_out, a, c);
  and and_3 (and_3_out, b, c);
  or or_1 (t, and_1_out, and_2_out, and_3_out);
endmodule
