// Logisim project exp1_4.circ as structural Verilog: 1 circuit, main circuit main
module main (
  input  d0,
  input  d1,
  input  d2,
  input  d3,
  input  s0,
  input  s1,
  output y
);

  wire nand_1_out, nand_2_out, nand_3_out, nand_4_out, nand_5_out, nand_6_out, nand_7_out, nand_8_out;

  nand nand_1 (nand_1_out, s1, s1);
  nand nand_2 (nand_2_out, s0, s0);
  nand nand_3 (nand_3_out, s1, s1);
  nand nand_4 (nand_4_out, s0, s0);
  nand nand_5 (nand_5_out, d0, nand_1_out, nand_2_out);
  nand nand_6 (nand_6_out, d1, nand_3_out, s0);
  nand nand_7 (nand_7_out, d2, s1, nand_4_out);
  nand nand_8 (nand_8_out, d3, s1, s0);
  nand nand_9 (y, nand_5_out, nand_6_out, nand_7_out, nand_8_out);
endmodule
